# Fritzing sketch Pflanzen-waessern Schaltplan 2 (saved by Fritzing 0.9.3b)
circuit board: 8.46667cm x 5.64444cm

parts:
  Nano = Arduino Nano (Rev3.0) (ICSP)
  Feuchtigkeits-Sensor1 = Soil Moisture Sensor
  Feuchtigkeits-Sensor2 = Soil Moisture Sensor
  Pumpe_1 = DC Motor
  Freilaufdiode_1 = Diode [package=diode-1n4148]
  Freilaufdiode_2 = Diode [package=diode-1n4148]
  Transistor_1 = NPN-Transistor [package="TO92 [THT]"]
  R1 = Resistor [tolerance=±5% resistance=1k package="2010 [SMD]"]
  Transistor_2 = NPN-Transistor [package="TO92 [THT]"]
  R2 = Resistor [tolerance=±5% resistance=1k package="2010 [SMD]"]
  R3 = Resistor [tolerance=±5% resistance=220 package="2010 [SMD]"]
  R4 = Resistor [tolerance=±5% resistance=220 package="2010 [SMD]"]
  Pumpe_2 = DC Motor

nets:
  GND: Nano.GND, Feuchtigkeits-Sensor1.GND, Feuchtigkeits-Sensor2.GND, R3.Pin_0, R4.Pin_0
  VCC: Nano.5V, Feuchtigkeits-Sensor1.VCC, Feuchtigkeits-Sensor2.VCC, Pumpe_1.pin_1, Freilaufdiode_1.C, Freilaufdiode_2.C, Pumpe_2.pin_1
  N1: Nano.A3, R2.Pin_0
  N2: Nano.A2, R1.Pin_0
  N3: Nano.A1, Feuchtigkeits-Sensor2.SIG
  N4: Nano.A0, Feuchtigkeits-Sensor1.SIG
  N5: Pumpe_1.pin_2, Freilaufdiode_1.A, Transistor_1.C
  N6: Freilaufdiode_2.A, Transistor_2.C, Pumpe_2.pin_2
  N7: Transistor_1.E, R3.Pin_1
  N8: Transistor_1.B, R1.Pin_1
  N9: Transistor_2.E, R4.Pin_1
  N10: Transistor_2.B, R2.Pin_1
