# Fritzing sketch Pflanzen-waessern Schaltplan 5_ 1 Motor (saved by Fritzing 0.9.3b)
circuit board: 8.46667cm x 5.64444cm
breadboards: 1

parts:
  Nano = Arduino Nano (Rev3.0) (ICSP)
  Feuchtigkeits-Sensor1 = Soil Moisture Sensor
  Pumpe_1 = DC Motor
  Transistor_1 = NPN-Transistor [package="TO92 [THT]"]
  R3 = Resistor [tolerance=±5% resistance=220 package="2010 [SMD]"]
  R4 = Resistor [tolerance=±5% resistance=220 package=THT]
  D1 = Rectifier Diode [part_number=1N4001 package="300 mil [THT]"]
  VCC1 = Battery block 9V

nets:
  GND: Nano.GND, Feuchtigkeits-Sensor1.GND, R3.Pin_0, VCC1.-
  N1: Nano.VIN, VCC1.+
  5V: Nano.5V, Feuchtigkeits-Sensor1.VCC, Pumpe_1.pin_1, D1.cathode
  N2: Nano.A1, R4.Pin_0
  N3: Nano.A0, Feuchtigkeits-Sensor1.SIG
  N4: Pumpe_1.pin_2, Transistor_1.C, D1.anode
  N5: Transistor_1.E, R3.Pin_1
  N6: Transistor_1.B, R4.Pin_1

// code stored in the sketch: Pflanzen-waessern.ino
/*
  Analog Input

  This example code is in the public domain.

  http://www.arduino.cc/en/Tutorial/AnalogInput
*/

int sensorPin = A0;    // select the input pin for the potentiometer
int ledPin = 13;      // select the pin for the LED
int FeuchtigkeitsSensor = 0;  // variable to store the value coming from the sensor
int motorPin = A1; // PWM for 5V pump

void setup() {
  // declare the ledPin as an OUTPUT:
  pinMode(ledPin, OUTPUT);
  pinMode(sensorPin, INPUT);
  Serial.begin(9600);
}

void loop() {
  // read the value from the sensor:
  FeuchtigkeitsSensor = analogRead(sensorPin);
  Serial.println(FeuchtigkeitsSensor);
  
// 800 und 900 trockene erde --> pumpe an--> pause 5 Sek
// 700 geht noch so  --> pumpe langsamer --> pause 5 Sek
// 600 gut feucht    --> pumpe langsamer --> pause 4 Sek
// 350 450 feucht - genau richtig --> pumpe aus
// 300 zu gut stopp --> pumpe aus
// schlafe 2h  
  if ( FeuchtigkeitsSensor > 800 ) 
  {
      pumpe(1, 10, 100 );
  }
  else if (FeuchtigkeitsSensor > 700)
  {
      pumpe(1, 8, 100 );
  }
  else if (FeuchtigkeitsSensor > 600)
  {
      pumpe(1, 4 ,80);
  }
  else if (FeuchtigkeitsSensor > 450)
  {
      pumpe(1, 4 ,50);
  }
  else if (FeuchtigkeitsSensor > 350)
  {
      pumpe(0, 3600 , 0);
  }
  else
  {
      pumpe(0, 7200 , 0);
  }  


}

void pumpe (int zustand, int dauer, int speed ) {
  if (zustand > 0 ){
    motor (1,speed);
    digitalWrite(ledPin, HIGH);
  }
  else
  {
    motor (0,0);
    digitalWrite(ledPin, LOW);
  }
  delay(dauer * 1000);
}

void motor (int zustand, int speed ){

}
